# Fritzing sketch fluval_led_control (saved by Fritzing 0.9.2b)
circuit board: 8.46667cm x 5.64444cm
breadboards: 1

parts:
  U1 = NodeMCU V1.0
  OLED = OLED 0.96" 128x64 I2C SSD1306
  T1 = TMP36 Temperature Sensor [package="TO92 [THT]"]
  LED1 = LED - 3mm [color="Infrared (850nm)" package="3 mm [THT]"]
  T2 = TMP36 [package=to-92-kit]
  R2 = Resistor [tolerance=±5% resistance=150 package=THT]
  R1 = Resistor [tolerance=±5% resistance=220 package=THT]

nets:
  N1: U1.D2, LED1.anode
  N2: U1.D3, OLED.SCA
  N3: U1.D4, T1.Vout, R2.Pin_1
  VCC: U1.3V3, OLED.VCC, T1.+Vs, T2.VCC, R2.Pin_0
  GND: U1.GND, OLED.GND, T1.GND, T2.GND, R1.Pin_1
  N4: U1.D5, OLED.SCL
  N5: U1.A0, T2.VOUT
  N6: LED1.cathode, R1.Pin_0

custom parts:
  NodeMCU V1.0: ESP8266 based NodeMCU
